# Fritzing sketch ATmelProgrammer (saved by Fritzing 0.9.3b)
circuit board: 6.42191cm x 4.61749cm
breadboards: 1

parts:
  ZIF_SOCKET = Aries 28-6574-10 28W ZIF Socket [part_number=28-6574-10]
  XTAL1 = Crystal [frequency="16 Mhz" package=THT]
  C1 = Ceramic Capacitor [capacitance=22pF package="100 mil [THT, multilayer]"]
  C2 = Ceramic Capacitor [capacitance=22pF package="100 mil [THT, multilayer]"]
  Arduino_Nano = Arduino Nano (Rev3.0)
  C3 = Electrolytic Capacitor [capacitance=10µF package="100 mil [THT, electrolytic]"]
  SW3 = DIP SWITCH [package=dipswitch-02]
  SW1 = DIP SWITCH [package=dipswitch-02]
  SW2 = DIP SWITCH [package=dipswitch-02]

nets:
  N1: ZIF_SOCKET.Pin_1, SW1.2
  N2: ZIF_SOCKET.Pin_4, SW1.1
  N3: ZIF_SOCKET.Pin_7, Arduino_Nano.5V, SW3.1
  N4: ZIF_SOCKET.Pin_8, C1.1, C2.0, Arduino_Nano.GND, SW1.4
  N5: ZIF_SOCKET.Pin_9, XTAL1.pin_0, C1.0
  N6: ZIF_SOCKET.Pin_10, XTAL1.pin_1, C2.1
  N7: ZIF_SOCKET.Pin_17, Arduino_Nano.D11/MOSI, SW2.1
  N8: ZIF_SOCKET.Pin_18, Arduino_Nano.D12/MISO, SW2.2
  N9: ZIF_SOCKET.Pin_19, Arduino_Nano.D13/SCK, SW3.2
  N10: ZIF_SOCKET.Pin_25, SW2.4
  N11: ZIF_SOCKET.Pin_26, SW2.3
  N12: ZIF_SOCKET.Pin_27, SW3.3
  N13: ZIF_SOCKET.Pin_28, SW3.4
  N14: Arduino_Nano.RESET, C3.+
  N15: Arduino_Nano.D10, SW1.3

notes:
  E
  A
  B
  C
  D
  F
  Jumpers/Switches
  Atmega328:
  All Off, except F
  ATtiny85:
  All On
