# Fritzing sketch SmartCarControllerHat-smt (saved by Fritzing 0.9.3b)
circuit board: 6.5377cm x 3.39098cm

parts:
  J4 = female pin header, 6 pins [form="♀ (female)"]
  J5 = female pin header, 6 pins [form="♀ (female)"]
  J6 = female pin header, 6 pins [form="♀ (female)"]
  J9 = double row female pin header, 6 pins [form="♀ (female)"]
  IC6 = SO14 [chip_label=ATTiny24/44/84 package=SO]
  J10 = double row female pin header, 8 pins [form="♀ (female)"]
  Composant2 = SO08 [chip_label=L293DD-TOP package=SO]
  Composant3 = SO08 [chip_label=L293DD-BOTTOM package=SO]
  J11 = female pin header, 3 pins [form="♀ (female)"]
  R1 = Resistor [tolerance=±5% resistance=10k package="0805 [SMD]"]
  Y4 = Resonator [part_number="CSTCE 16M0V53" package=resonator-smd]
  R2 = Resistor [tolerance=±5% resistance=10k package="0805 [SMD]"]
  J12 = female pin header, 3 pins [form="♀ (female)"]
  J13 = female pin header, 3 pins [form="♀ (female)"]
  U3 = atmega168 smd [package=tqfp]
  J14 = double row female pin header, 40 pins [form="♀ (female)"]

nets:
  N1: J4.pin1, J4.pin2, J4.pin3, J4.pin4, J4.pin5, J4.pin6, J9.pin2, J9.pin5, J11.pin2
  N2: J5.pin1, J5.pin2, J5.pin3, J5.pin4, J5.pin5, J5.pin6, J9.pin3, J9.pin4, IC6.14, J10.pin1, J10.pin2, J10.pin3, J10.pin4, Composant2.4, Composant3.1, J11.pin3, J14.pin33
  N3: J6.pin1, U3.Pin_32
  N4: J6.pin2, U3.Pin_1
  N5: J6.pin3, U3.Pin_2
  N6: J6.pin4, U3.Pin_9
  N7: J6.pin5, U3.Pin_10
  N8: J6.pin6, U3.Pin_11
  N9: J9.pin1, IC6.2
  N10: J9.pin6, IC6.3
  N11: IC6.1, Composant2.1, Composant2.8, Composant3.5, R1.Pin_0, J14.pin19
  N12: IC6.4, R1.Pin_1, J14.pin32
  N13: IC6.5, U3.Pin_12
  N14: IC6.7, J14.pin31
  N15: IC6.8, J14.pin26
  N16: IC6.9, J14.pin30
  N17: IC6.10, Composant2.7
  N18: IC6.11, Composant3.6
  N19: IC6.12, Composant3.3
  N20: IC6.13, Composant2.2
  N21: J10.pin5, Composant3.2
  N22: J10.pin6, Composant2.3
  N23: J10.pin7, Composant2.6
  N24: J10.pin8, Composant3.7
  N25: Composant2.5, Composant3.8
  N26: Composant3.4, J11.pin1
  N27: Y4.1, U3.Pin_7
  N28: Y4.2, U3.Pin_3, U3.Pin_5, U3.Pin_21, J14.pin40
  N29: Y4.3, U3.Pin_8
  N30: R2.Pin_0, U3.Pin_29, J14.pin1
  N31: R2.Pin_1, U3.Pin_4, U3.Pin_6, U3.Pin_18, J14.pin20
  N32: J12.pin1, U3.Pin_26
  N33: J12.pin2, U3.Pin_27
  N34: J12.pin3, U3.Pin_28
  N35: J13.pin1, U3.Pin_25
  N36: J13.pin2, U3.Pin_24
  N37: J13.pin3, U3.Pin_23
  N38: U3.Pin_15, J14.pin36
  N39: U3.Pin_16, J14.pin35
  N40: U3.Pin_17, J14.pin34
  N41: U3.Pin_30, J14.pin17
  N42: U3.Pin_31, J14.pin16

notes:
  right wheel pwm out
  left wheel pwm out
  right wheel speed encoder IN
  serial cmd in
  +5V Gnd Gnd +12V
  left wheel speed encoder IN
  right wheel 0v
  left wheel 0v
  right wheel +12v
  left wheel +12v
  digital out 0-4 0v
  digital out 0-4 +12v
  GND
  +5v
  +12v
