# Fritzing sketch lcd1602 (saved by Fritzing 0.9.3b)
circuit board: 6.09091cm x 4.83843cm
breadboards: 1

parts:
  LCD1 = LCD screen [part_number=QY-1602A]
  Composant1 = Arduino Pro Mini (5V)
  R1 = Rotary Potentiometer (Large) [maximum_resistance=100kΩ package=THT]
  J1 = female pin header, 10 pins [form="♀ (female)"]

nets:
  VSS: LCD1.VSS, LCD1.R/W, LCD1.LED-, Composant1.GND, R1.leg1, J1.pin4
  VDD: LCD1.VDD, LCD1.LED+, Composant1.VCC, R1.leg2, J1.pin6
  N1: LCD1.V0, R1.wiper
  N2: LCD1.RS, Composant1.D2
  N3: LCD1.E, Composant1.D3
  N4: LCD1.DB4, Composant1.D4
  N5: LCD1.DB5, Composant1.D5
  N6: LCD1.DB6, Composant1.D6
  N7: LCD1.DB7, Composant1.D7
  N8: Composant1.TXO, J1.pin2
  N9: Composant1.RXI, J1.pin1
  N10: Composant1.RAW, J1.pin3
  N11: Composant1.RESET, J1.pin5
  N12: Composant1.SCK, J1.pin7
  N13: Composant1.MISO, J1.pin8
  N14: Composant1.MOSI, J1.pin9
  N15: Composant1.D10, J1.pin10
